# Fritzing sketch gps (saved by Fritzing 0.9.5d)
breadboards: 1

parts:
  Part1 = Arduino Uno (Rev3)
  NEO-6M-0-001 = SUP500F [package=sup500f]
  MicroSD_Card_Adapter = MicroSD Card Module

nets:
  N1: Part1.D10_PWM/SS, MicroSD_Card_Adapter.CS
  N2: Part1.D11_PWM/MOSI, MicroSD_Card_Adapter.MOSI
  N3: Part1.D12/MISO, MicroSD_Card_Adapter.MISO
  N4: Part1.D13/SCK, MicroSD_Card_Adapter.SCK
  N5: Part1.D3_PWM, NEO-6M-0-001.RX-I
  N6: Part1.D4, NEO-6M-0-001.TX-O
  VCC: Part1.5V, NEO-6M-0-001.VCC, MicroSD_Card_Adapter.VCC
  GND: Part1.GND, NEO-6M-0-001.GND, MicroSD_Card_Adapter.GND
